// Logisim project L293D_Logisim_Evolution.circ as structural Verilog: 1 circuit, main circuit L293D
module L293D (
  input  VCC2,
  input  Enable1,
  input  Input2,
  input  Input1,
  input  GND1,
  input  GND2,
  input  VCC1,
  input  Enable2,
  input  Input3,
  input  Input4,
  input  GND3,
  input  GND4,
  output Output1,
  output Output2,
  output Output3,
  output Output4
);

  wire and_1_out, and_2_out, and_3_out, and_4_out;

  and and_1 (and_1_out, Enable1, Input1);
  and and_2 (and_2_out, Enable2, Input3);
  Transistor transistor_1 (.in(VCC2), .out(Output1), .gate(and_1_out));
  Transistor #(.\type ("n")) transistor_2 (.in(GND1), .out(Output1), .gate(and_1_out));
  Transistor transistor_3 (.in(VCC2), .out(Output3), .gate(and_2_out));
  Transistor #(.\type ("n")) transistor_4 (.in(GND1), .out(Output3), .gate(and_2_out));
  Transistor transistor_5 (.in(VCC2), .out(Output2), .gate(and_3_out));
  Transistor #(.\type ("n")) transistor_6 (.in(GND1), .out(Output2), .gate(and_3_out));
  Transistor transistor_7 (.in(VCC2), .out(Output4), .gate(and_4_out));
  Transistor #(.\type ("n")) transistor_8 (.in(GND1), .out(Output4), .gate(and_4_out));
  and and_3 (and_3_out, Enable1, Input2);
  and and_4 (and_4_out, Enable2, Input4);

  assign GND2 = GND1;
  assign GND3 = GND1;
  assign GND4 = GND1;
endmodule
